// Logisim project cir.circ as structural Verilog
module main (
  input  in_1,
  input  in_2,
  input  in_3,
  output out_4
);
endmodule

module main_1 (
);

  wire main_1_out_4, undriven, undriven_2, undriven_3;

  main main_1 (.in_1(undriven), .in_2(undriven_2), .out_4(main_1_out_4), .in_3(undriven_3));
endmodule
